// Logisim project SmartWaterTank.circ as structural Verilog: 1 circuit, main circuit main
module main (
  input  H_HighLevel,
  input  O_Overflow,
  input  L_LowLevel,
  output Pump,
  output Buzzer
);

  wire Safe___NOT_H_OR_O_out;

  nor Safe___NOT_H_OR_O (Safe___NOT_H_OR_O_out, H_HighLevel, O_Overflow);
  and Pump___L_AND_Safe (Pump, Safe___NOT_H_OR_O_out, L_LowLevel);

  assign Buzzer = O_Overflow;
endmodule
